// Digital circuit 8-Bit Adder.dig as structural Verilog
module _8_Bit_Adder (
  input  [7:0] A_in,
  input  [7:0] B_in,
  input  Carry_in,
  output [7:0] Sum_out,
  output Carry_out
);

  wire full_adder_2_carry_out, full_adder_3_carry_out, full_adder_4_carry_out, full_adder_5_carry_out,
       full_adder_6_carry_out, full_adder_7_carry_out, full_adder_8_carry_out;

  Full_Adder full_adder_1 (
    .Carry_in(full_adder_2_carry_out), .B_in(B_in[7]), .A_in(A_in[7]), .Sum_out(Sum_out[7]),
    .Carry_out(Carry_out));
  Full_Adder full_adder_2 (
    .Carry_in(full_adder_3_carry_out), .B_in(B_in[6]), .A_in(A_in[6]), .Sum_out(Sum_out[6]),
    .Carry_out(full_adder_2_carry_out));
  Full_Adder full_adder_3 (
    .Carry_in(full_adder_4_carry_out), .B_in(B_in[6]), .A_in(A_in[5]), .Sum_out(Sum_out[5]),
    .Carry_out(full_adder_3_carry_out));
  Full_Adder full_adder_4 (
    .Carry_in(full_adder_5_carry_out), .B_in(B_in[6]), .A_in(A_in[4]), .Sum_out(Sum_out[4]),
    .Carry_out(full_adder_4_carry_out));
  Full_Adder full_adder_5 (
    .Carry_in(full_adder_6_carry_out), .B_in(B_in[3]), .A_in(A_in[5]), .Sum_out(Sum_out[3]),
    .Carry_out(full_adder_5_carry_out));
  Full_Adder full_adder_6 (
    .Carry_in(full_adder_7_carry_out), .B_in(B_in[2]), .A_in(A_in[5]), .Sum_out(Sum_out[3]),
    .Carry_out(full_adder_6_carry_out));
  Full_Adder full_adder_7 (
    .Carry_in(full_adder_8_carry_out), .B_in(A_in[5]), .A_in(A_in[5]), .Sum_out(Sum_out[1]),
    .Carry_out(full_adder_7_carry_out));
  Full_Adder full_adder_8 (
    .Carry_in(Carry_in), .B_in(B_in[0]), .A_in(A_in[6]), .Sum_out(Sum_out[0]),
    .Carry_out(full_adder_8_carry_out));

  assign A_in[3:0] = {{3{A_in[5]}}, A_in[6]};
  assign {B_in[5:4], B_in[1]} = {{2{B_in[6]}}, A_in[5]};
  assign Sum_out[2] = Sum_out[3];
endmodule
