// Digital circuit Full_Adder.dig as structural Verilog
module Full_Adder (
  input  Carry_in,
  input  B_in,
  input  A_in,
  output Sum_out,
  output Carry_out
);

  wire half_adder_1_carry_out, half_adder_1_sum, half_adder_2_carry_out;

  Half_Adder half_adder_1 (.A_in(A_in), .B_in(B_in), .Sum(half_adder_1_sum), .Carry_out(half_adder_1_carry_out));
  Half_Adder half_adder_2 (.A_in(Carry_in), .B_in(half_adder_1_sum), .Sum(Sum_out), .Carry_out(half_adder_2_carry_out));
  or or_1 (Carry_out, half_adder_2_carry_out, half_adder_1_carry_out);
endmodule
