// Digital circuit Half Adder.dig as structural Verilog
module Half_Adder (
  input  A_in,
  input  B_in,
  output Sum,
  output Sum_out
);

  xor xor_1 (Sum, A_in, B_in);
  and and_1 (Sum_out, A_in, B_in);
endmodule
